# Fritzing sketch setup (saved by Fritzing 0.9.4)
breadboards: 1

parts:
  Tx_Control_Unit = Arduino Uno (Rev3) - ICSP
  Rx_Control_Unit = Arduino Uno (Rev3) - ICSP
  U1 = 4001 4 x 2 Input NOR Gate [part_number=4001 package="DIP (Dual Inline) [THT]"]  # not connected
  U1_1 = 4001_4_x_2_input_NOR_gate_multipart_subpart2 [part_number=4001]
  Q1 = TRANSISTOR_NPN [package=to-92]
  LED1 = smd LED [color="Infrared (940nm)" package="0805 [SMD]"]
  R2 = Resistor [tolerance=±5% resistance=10k package=THT]
  R2_2 = Resistor [tolerance=±5% resistance=47 package=THT]
  TSOP98638 = TSOP312.., 314.. [package=THT]
  C1 = Electrolytic Capacitor [capacitance=4.7µF package="0807 [SMD, electrolytic]"]
  R3 = Resistor [tolerance=±5% resistance=100 package=THT]

nets:
  N1: Tx_Control_Unit.5V, R2_2.Pin_0
  N2: Tx_Control_Unit.GND, Q1.E
  N3: Tx_Control_Unit.D11_PWM/MOSI, U1_1.connector1
  N4: Tx_Control_Unit.D1/TX, U1_1.connector0
  GND: Rx_Control_Unit.GND, TSOP98638.GND, C1.-
  N5: Rx_Control_Unit.D0/RX, TSOP98638.Data, C1.+, R3.Pin_0
  N6: Rx_Control_Unit.3V3, TSOP98638.Vs, R3.Pin_1
  N7: U1_1.connector2, R2.Pin_0
  N8: Q1.B, R2.Pin_1
  N9: Q1.C, LED1.cathode
  N10: LED1.anode, R2_2.Pin_1
